// Logisim project 1_Bit_Register.circ as structural Verilog: 1 circuit, main circuit main
module main (
  input  Load,
  input  Data,
  input  Output_Ctrl,
  input  Clock
);

  wire and_1_out, and_2_out, D_Flip_Flop_q, not_1_out, or_1_out, tri_state_logic_out;

  not not_1 (not_1_out, Load);
  and and_1 (and_1_out, D_Flip_Flop_q, not_1_out);
  and and_2 (and_2_out, Load, Data);
  or or_1 (or_1_out, and_1_out, and_2_out);
  D_Flip_Flop D_Flip_Flop (.D(or_1_out), .clk(Clock), .Q(D_Flip_Flop_q));  // open: Qn, preset, reset
  assign tri_state_logic_out = Output_Ctrl ? D_Flip_Flop_q : 1'bz;  // Controlled_Buffer tri_state_logic
  LED led_1 (.in(tri_state_logic_out));

  // Notes on the sheet:
  //   1-Bit Register Diagram
  //   to control the sink/source states
  //   Clock has 4 options: Rising Edge, Falling Edge, Higher, Lower
  //   Output_Ctrl: a single register cell also has a Tri-state output control gate, with output control logic on top,
  //   truth table
  //   Load     Data    Output
  //   0            0          0
  //   0            1          0
  //   1            0          0
  //   1            1          1
endmodule
