// Logisim project 4_Bit_Full_Adder.circ as structural Verilog: 1 circuit, main circuit main
module main (
  input  A1,
  input  B1,
  input  CI,
  input  A_1,
  input  A_2,
  input  A2,
  input  A_3,
  input  A_4,
  input  B2,
  input  B_1,
  input  A3,
  input  B_2,
  input  B_3,
  input  B3,
  input  B_4,
  input  A4,
  input  B4
);

  wire and_1_out, and_2_out, and_3_out, and_4_out, and_5_out, and_6_out, and_7_out, and_8_out, n74283_1_pin1,
       n74283_1_pin4, n74283_1_pin9, n74283_1_pin10, n74283_1_pin13, or_1_out, or_2_out, or_3_out, or_4_out,
       xor_1_out, xor_2_out, xor_3_out, xor_4_out, xor_5_out, xor_6_out, xor_7_out, xor_8_out;

  xor xor_1 (xor_1_out, A1, B1);
  and and_1 (and_1_out, A1, B1);
  xor xor_2 (xor_2_out, A2, B2);
  and and_2 (and_2_out, A2, B2);
  xor xor_3 (xor_3_out, A3, B3);
  and and_3 (and_3_out, A3, B3);
  xor xor_4 (xor_4_out, A4, B4);
  and and_4 (and_4_out, A4, B4);
  xor xor_5 (xor_5_out, xor_1_out, CI);
  and and_5 (and_5_out, xor_1_out, CI);
  xor xor_6 (xor_6_out, xor_2_out, or_1_out);
  and and_6 (and_6_out, xor_2_out, or_1_out);
  xor xor_7 (xor_7_out, xor_3_out, or_2_out);
  and and_7 (and_7_out, xor_3_out, or_2_out);
  xor xor_8 (xor_8_out, xor_4_out, or_3_out);
  and and_8 (and_8_out, xor_4_out, or_3_out);
  LED led_1 (.in(xor_5_out));
  or or_1 (or_1_out, and_1_out, and_5_out);
  LED led_2 (.in(xor_6_out));
  or or_2 (or_2_out, and_2_out, and_6_out);
  LED led_3 (.in(xor_7_out));
  or or_3 (or_3_out, and_3_out, and_7_out);
  LED led_4 (.in(xor_8_out));
  or or_4 (or_4_out, and_4_out, and_8_out);
  LED led_5 (.in(or_4_out));
  _74283 u_74283_1 (
    .pin1(n74283_1_pin1), .pin2(B_2), .pin3(A_2), .pin4(n74283_1_pin4), .pin5(A_1), .pin6(B_1), .pin15(B_3),
    .pin14(A_3), .pin13(n74283_1_pin13), .pin12(A_4), .pin11(B_4), .pin10(n74283_1_pin10),
    .pin9(n74283_1_pin9));  // open: pin7
  LED led_6 (.in(n74283_1_pin4));
  LED led_7 (.in(n74283_1_pin1));
  LED led_8 (.in(n74283_1_pin13));
  LED led_9 (.in(n74283_1_pin10));
  LED led_10 (.in(n74283_1_pin9));

  // Notes on the sheet:
  //   4_Bit_Full_Adder
  //   Input A
  //   Input B
  //   4_Bit_Full_Adder_Chip
  //   Output
endmodule
