// Logisim project 4_Bit_Registers_And_Adder.circ as structural Verilog: 1 circuit, main circuit main
module main (
  input  Load,
  input  a0,
  input  Output_Ctrl,
  input  CI,
  input  Clock,
  input  a1,
  input  a2,
  input  a3,
  input  Load_B,
  input  b0,
  input  Output_Ctrl_B,
  input  Clock_B,
  input  b1,
  input  b2,
  input  b3
);

  wire and_1_out, and_2_out, and_3_out, and_4_out, and_5_out, and_6_out, and_7_out, and_8_out, and_9_out,
       and_10_out, and_11_out, and_12_out, and_13_out, and_14_out, and_15_out, and_16_out, and_17_out,
       and_18_out, and_19_out, and_20_out, and_21_out, and_22_out, and_23_out, and_24_out,
       controlled_buffer_1_out, controlled_buffer_2_out, controlled_buffer_3_out, controlled_buffer_4_out,
       controlled_buffer_5_out, controlled_buffer_6_out, d_ff_1_q, d_ff_2_q, d_ff_3_q, d_ff_4_q, d_ff_5_q,
       d_ff_6_q, D_Flip_Flop_B_q, D_Flip_Flop_q, not_1_out, not_2_out, not_3_out, not_4_out, not_5_out,
       not_6_out, not_7_out, not_8_out, or_1_out, or_2_out, or_3_out, or_4_out, or_5_out, or_6_out, or_7_out,
       or_8_out, or_9_out, or_10_out, or_11_out, or_12_out, tri_state_logic_B_out, tri_state_logic_out,
       xor_1_out, xor_2_out, xor_3_out, xor_4_out, xor_5_out, xor_6_out, xor_7_out, xor_8_out;

  not not_1 (not_1_out, Load);
  and and_1 (and_1_out, D_Flip_Flop_q, not_1_out);
  and and_2 (and_2_out, Load, a0);
  not not_2 (not_2_out, Load);
  and and_3 (and_3_out, D_Flip_Flop_B_q, not_3_out);
  not not_3 (not_3_out, Load_B);
  and and_4 (and_4_out, Load_B, b0);
  and and_5 (and_5_out, d_ff_1_q, not_2_out);
  and and_6 (and_6_out, Load, a1);
  and and_7 (and_7_out, d_ff_2_q, not_4_out);
  not not_4 (not_4_out, Load);
  and and_8 (and_8_out, Load, a2);
  and and_9 (and_9_out, d_ff_3_q, not_5_out);
  not not_5 (not_5_out, Load);
  and and_10 (and_10_out, Load, a3);
  and and_11 (and_11_out, d_ff_4_q, not_6_out);
  not not_6 (not_6_out, Load_B);
  and and_12 (and_12_out, Load_B, b1);
  not not_7 (not_7_out, Load_B);
  not not_8 (not_8_out, Load_B);
  or or_1 (or_1_out, and_1_out, and_2_out);
  or or_2 (or_2_out, and_3_out, and_4_out);
  and and_13 (and_13_out, d_ff_5_q, not_7_out);
  and and_14 (and_14_out, Load_B, b2);
  and and_15 (and_15_out, d_ff_6_q, not_8_out);
  and and_16 (and_16_out, Load_B, b3);
  D_Flip_Flop D_Flip_Flop (.D(or_1_out), .clk(Clock), .Q(D_Flip_Flop_q));  // open: Qn, preset, reset
  or or_3 (or_3_out, and_5_out, and_6_out);
  or or_4 (or_4_out, and_7_out, and_8_out);
  or or_5 (or_5_out, and_9_out, and_10_out);
  D_Flip_Flop D_Flip_Flop_B (.D(or_2_out), .clk(Clock_B), .Q(D_Flip_Flop_B_q));  // open: Qn, preset, reset
  or or_6 (or_6_out, and_11_out, and_12_out);
  or or_7 (or_7_out, and_13_out, and_14_out);
  or or_8 (or_8_out, and_15_out, and_16_out);
  assign tri_state_logic_out = Output_Ctrl ? D_Flip_Flop_q : 1'bz;  // Controlled_Buffer tri_state_logic
  D_Flip_Flop d_ff_1 (.D(or_3_out), .clk(Clock), .Q(d_ff_1_q));  // open: Qn, preset, reset
  D_Flip_Flop d_ff_2 (.D(or_4_out), .clk(Clock), .Q(d_ff_2_q));  // open: Qn, preset, reset
  D_Flip_Flop d_ff_3 (.D(or_5_out), .clk(Clock), .Q(d_ff_3_q));  // open: Qn, preset, reset
  assign tri_state_logic_B_out = Output_Ctrl_B ? D_Flip_Flop_B_q : 1'bz;  // Controlled_Buffer tri_state_logic_B
  D_Flip_Flop d_ff_4 (.D(or_6_out), .clk(Clock_B), .Q(d_ff_4_q));  // open: Qn, preset, reset
  D_Flip_Flop d_ff_5 (.D(or_7_out), .clk(Clock_B), .Q(d_ff_5_q));  // open: Qn, preset, reset
  D_Flip_Flop d_ff_6 (.D(or_8_out), .clk(Clock_B), .Q(d_ff_6_q));  // open: Qn, preset, reset
  assign controlled_buffer_1_out = Output_Ctrl ? d_ff_1_q : 1'bz;  // Controlled_Buffer controlled_buffer_1
  assign controlled_buffer_2_out = Output_Ctrl ? d_ff_2_q : 1'bz;  // Controlled_Buffer controlled_buffer_2
  assign controlled_buffer_3_out = Output_Ctrl ? d_ff_3_q : 1'bz;  // Controlled_Buffer controlled_buffer_3
  assign controlled_buffer_4_out = Output_Ctrl_B ? d_ff_4_q : 1'bz;  // Controlled_Buffer controlled_buffer_4
  LED led_1 (.in(tri_state_logic_out));
  LED led_2 (.in(controlled_buffer_1_out));
  LED led_3 (.in(controlled_buffer_2_out));
  LED led_4 (.in(controlled_buffer_3_out));
  assign controlled_buffer_5_out = Output_Ctrl_B ? d_ff_5_q : 1'bz;  // Controlled_Buffer controlled_buffer_5
  assign controlled_buffer_6_out = Output_Ctrl_B ? d_ff_6_q : 1'bz;  // Controlled_Buffer controlled_buffer_6
  LED led_5 (.in(tri_state_logic_B_out));
  LED led_6 (.in(controlled_buffer_4_out));
  LED led_7 (.in(controlled_buffer_5_out));
  LED led_8 (.in(controlled_buffer_6_out));
  xor xor_1 (xor_1_out, tri_state_logic_out, tri_state_logic_B_out);
  and and_17 (and_17_out, tri_state_logic_out, tri_state_logic_B_out);
  xor xor_2 (xor_2_out, controlled_buffer_1_out, controlled_buffer_4_out);
  and and_18 (and_18_out, controlled_buffer_1_out, controlled_buffer_4_out);
  xor xor_3 (xor_3_out, controlled_buffer_2_out, controlled_buffer_5_out);
  and and_19 (and_19_out, controlled_buffer_2_out, controlled_buffer_5_out);
  xor xor_4 (xor_4_out, controlled_buffer_3_out, controlled_buffer_6_out);
  and and_20 (and_20_out, controlled_buffer_3_out, controlled_buffer_6_out);
  xor xor_5 (xor_5_out, xor_1_out, CI);
  and and_21 (and_21_out, xor_1_out, CI);
  or or_9 (or_9_out, and_17_out, and_21_out);
  xor xor_6 (xor_6_out, xor_2_out, or_9_out);
  and and_22 (and_22_out, xor_2_out, or_9_out);
  or or_10 (or_10_out, and_18_out, and_22_out);
  xor xor_7 (xor_7_out, xor_3_out, or_10_out);
  and and_23 (and_23_out, xor_3_out, or_10_out);
  or or_11 (or_11_out, and_19_out, and_23_out);
  xor xor_8 (xor_8_out, xor_4_out, or_11_out);
  and and_24 (and_24_out, xor_4_out, or_11_out);
  or or_12 (or_12_out, and_20_out, and_24_out);
  LED led_9 (.in(xor_5_out));
  LED led_10 (.in(xor_6_out));
  LED led_11 (.in(xor_7_out));
  LED led_12 (.in(xor_8_out));
  LED led_13 (.in(or_12_out));

  // Notes on the sheet:
  //   REGISTER A
  //   REGISTER B
  //   4 Bit Registers and a 4 Bit Adder
  //   4_Bit_Full_Adder
endmodule
