// Logisim project Address_Decoder.circ as structural Verilog: 1 circuit, main circuit main
module main (
  input  A0,
  input  A1,
  input  A2,
  input  EN
);

  wire and_1_out, and_2_out, and_3_out, and_4_out, and_5_out, and_6_out, and_7_out, and_8_out, not_1_out,
       not_2_out, not_3_out;

  not not_1 (not_1_out, A0);
  not not_2 (not_2_out, A1);
  not not_3 (not_3_out, A2);
  and and_1 (and_1_out, not_1_out, not_2_out, not_3_out, EN);
  LED zero (.in(and_1_out));
  and and_2 (and_2_out, A0, not_2_out, not_3_out, EN);
  LED one (.in(and_2_out));
  and and_3 (and_3_out, not_1_out, A1, not_3_out, EN);
  LED two (.in(and_3_out));
  and and_4 (and_4_out, A0, A1, not_3_out, EN);
  LED three (.in(and_4_out));
  and and_5 (and_5_out, not_1_out, not_2_out, A2, EN);
  LED four (.in(and_5_out));
  and and_6 (and_6_out, A0, not_2_out, A2, EN);
  LED five (.in(and_6_out));
  and and_7 (and_7_out, not_1_out, A1, A2, EN);
  LED six (.in(and_7_out));
  and and_8 (and_8_out, A0, A1, A2, EN);
  LED seven (.in(and_8_out));

  // Notes on the sheet:
  //   Address Decoder 3-8 with Enable
endmodule
