// Logisim project D_Latch.circ as structural Verilog: 1 circuit, main circuit main
module main (
  input  Enable,
  input  Data
);

  wire and_1_out, and_2_out, nor_1_out, nor_2_out, not_1_out;

  not not_1 (not_1_out, Data);
  and and_1 (and_1_out, not_1_out, Enable);
  and and_2 (and_2_out, Enable, Data);
  nor nor_1 (nor_1_out, and_1_out, nor_2_out);
  nor nor_2 (nor_2_out, nor_1_out, and_2_out);
  LED led_1 (.in(nor_1_out));
endmodule
