// Logisim project Full_Adder_Diagram.circ as structural Verilog: 1 circuit, main circuit main
module main (
  input  A,
  input  B,
  input  CI
);

  wire and_1_out, and_2_out, or_1_out, xor_1_out, xor_2_out;

  _74283 u_74283_1 ();  // open: pin1, pin2, pin3, pin4, pin5, pin6, pin7, pin15, pin14, pin13, pin12, pin11, pin10, pin9
  xor xor_1 (xor_1_out, A, B);
  and and_1 (and_1_out, A, B);
  xor xor_2 (xor_2_out, xor_1_out, CI);
  and and_2 (and_2_out, xor_1_out, CI);
  or or_1 (or_1_out, and_2_out, and_1_out);
  LED Sum (.in(xor_2_out));
  LED Carry (.in(or_1_out));
  // XOR_Gate xor_3 is placed but not wired
  // AND_Gate and_3 is placed but not wired

  // Notes on the sheet:
  //   Full-Adder Diagram
  //   4_Bit_Adder Chip
  //   Sum Logic Gate: XOR
  //   Carry Logic Gate: AND
  //   Truth Table
  //   CI      A      B     SUM     CARRY
  //   0      0      0      0           0         
  //   0      0      1      1           0         
  //   0      1      0      1           0         
  //   0      1      1      0           1         
  //   1      0      0      1           0         
  //   1      0      1      0           1         
  //   1      1      0      0           1         
  //   1      1      1      1           1         
endmodule
