// Logisim project Full_Adder_and_Register_Excercise.circ as structural Verilog: 1 circuit, main circuit main
module main (
  input  A,
  input  B,
  input  CI,
  input  Load,
  input  Data,
  input  CLK,
  input  Output_Ctrl,
  input  L2,
  input  D2,
  input  OC2
);

  wire and_1_out, and_2_out, and_3_out, and_4_out, and_5_out, and_6_out, and_7_out, and_8_out, buffer_1_out,
       buffer_2_out, buffer_3_out, buffer_4_out, buffer_5_out, CLK2_out, controlled_buffer_1_out,
       controlled_buffer_2_out, d_ff_1_q, not_1_out, not_2_out, not_3_out, or_1_out, or_2_out, or_3_out,
       xor_1_out, xor_2_out, xor_3_out, xor_4_out;

  Clock CLK2 (.out(CLK2_out));
  and and_1 (and_1_out, Load, Data);
  not not_1 (not_1_out, L2);
  and and_2 (and_2_out, L2, D2);
  buf buffer_1 (buffer_1_out, CLK2_out);
  xor xor_1 (xor_1_out, A, B);
  and and_3 (and_3_out, A, B);
  and and_4 (and_4_out, d_ff_1_q, not_2_out);
  not not_2 (not_2_out, Load);
  and and_5 (and_5_out, buffer_4_out, not_1_out);
  and and_6 (and_6_out, xor_1_out, CI);
  or or_1 (or_1_out, and_4_out, and_1_out);
  or or_2 (or_2_out, and_5_out, and_2_out);
  xor xor_2 (xor_2_out, xor_1_out, CI);
  LED Sum (.in(xor_2_out));
  D_Flip_Flop d_ff_1 (.D(or_1_out), .clk(CLK), .Q(d_ff_1_q));  // open: Qn, preset, reset
  or or_3 (or_3_out, and_6_out, and_3_out);
  LED Carry (.in(or_3_out));
  and and_7 (and_7_out, or_2_out, buffer_1_out);
  and and_8 (and_8_out, buffer_1_out, not_3_out);
  not not_3 (not_3_out, or_2_out);
  assign controlled_buffer_1_out = Output_Ctrl ? d_ff_1_q : 1'bz;  // Controlled_Buffer controlled_buffer_1
  LED led_1 (.in(controlled_buffer_1_out));
  buf buffer_2 (buffer_2_out, and_7_out);
  buf buffer_3 (buffer_3_out, and_8_out);
  buf buffer_4 (buffer_4_out, xor_3_out);
  xor xor_3 (xor_3_out, buffer_2_out, buffer_5_out);
  xor xor_4 (xor_4_out, xor_3_out, buffer_3_out);
  buf buffer_5 (buffer_5_out, xor_4_out);
  assign controlled_buffer_2_out = OC2 ? xor_3_out : 1'bz;  // Controlled_Buffer controlled_buffer_2
  LED led_2 (.in(controlled_buffer_2_out));

  // Notes on the sheet:
  //   Full Adder
  //   1_Bit_Register
  //   Full Adder and Register
  //   1_Bit_Register with a D flip flop with gates
endmodule
