// Logisim project Half_Adder_Diagram.circ as structural Verilog: 1 circuit, main circuit main
module main (
  input  A,
  input  B
);

  wire and_1_out, xor_1_out;

  xor xor_1 (xor_1_out, A, B);
  and and_1 (and_1_out, A, B);
  LED Sum (.in(xor_1_out));
  LED Carry (.in(and_1_out));
  // XOR_Gate xor_2 is placed but not wired
  // AND_Gate and_2 is placed but not wired

  // Notes on the sheet:
  //   Half-Adder Diagram
  //   Sum Logic Gate: XOR
  //   Carry Logic Gate: AND
  //   Truth Table
  //   A      B     SUM     CARRY
  //   0      0      0           0         
  //   0      1      1           0         
  //   1      0      1           0         
  //   1      1      0           1         
endmodule
