// Logisim project Logic_Gates_with_transistors.circ as structural Verilog: 1 circuit, main circuit main
module main (
  input  in_1,
  input  in_2,
  input  in_3,
  input  in_4,
  input  in_5,
  input  in_6
);

  wire transistor_1_out, transistor_3_out, transistor_4_out;

  Transistor transistor_1 (.in(in_2), .out(transistor_1_out), .gate(in_1));
  Transistor transistor_2 (.in(in_2), .out(transistor_1_out), .gate(in_3));
  Transistor transistor_3 (.in(in_6), .out(transistor_3_out), .gate(in_4));
  LED led_1 (.in(transistor_1_out));
  Transistor transistor_4 (.in(transistor_3_out), .out(transistor_4_out), .gate(in_5));
  LED led_2 (.in(transistor_4_out));
  // OR_Gate or_1 is placed but not wired
  // AND_Gate and_1 is placed but not wired

  // Notes on the sheet:
  //   OR Gate
  //   Diagram:
  //   AND Gate
  //   Diagram:
  //   truth table
  //   A       B     OR
  //   0       0     0
  //   1       0     1
  //   0       1     1
  //   1       1     1
  //   truth table
  //   A       B     AND
  //   0       0     0
  //   1       0     0
  //   0       1     0
  //   1       1     1
endmodule
