// Logisim project Oscillator_Clock.circ as structural Verilog: 1 circuit, main circuit main
module main (
  input  Voltage,
  input  Selector
);

  wire and_1_out, and_2_out, not_1_out, not_2_out, or_1_out;

  not not_1 (not_1_out, Selector);
  and and_1 (and_1_out, Voltage, Selector);
  and and_2 (and_2_out, not_2_out, not_1_out);
  or or_1 (or_1_out, and_1_out, and_2_out);
  not not_2 (not_2_out, or_1_out);
  LED led_1 (.in(not_2_out));

  // Notes on the sheet:
  //   Oscillator
endmodule
