// Logisim project RAM_and_Address_Decoder.circ as structural Verilog: 1 circuit, main circuit main
module main (
  input  in_1,
  input  in_2,
  input  Data,
  input  in_4,
  input  in_5,
  input  in_6,
  input  in_7,
  input  in_8,
  input  Output_Ctrl,
  input  Clock,
  input  A0,
  input  A1,
  input  A2,
  input  EN,
  input  Output_Ctrl_2,
  input  Output_Ctrl_3,
  input  Output_Ctrl_4,
  input  Output_Ctrl_5,
  input  Output_Ctrl_6,
  input  Output_Ctrl_7,
  input  Output_Ctrl_8
);

  wire and_1_out, and_2_out, and_3_out, and_4_out, and_5_out, and_6_out, and_7_out, and_8_out, and_9_out,
       and_10_out, and_11_out, and_12_out, and_13_out, and_14_out, and_15_out, and_16_out, and_17_out,
       and_18_out, and_19_out, and_20_out, and_21_out, and_22_out, and_23_out, and_24_out, and_25_out,
       and_26_out, and_27_out, and_28_out, and_29_out, and_30_out, and_31_out, and_32_out, and_33_out,
       and_34_out, and_35_out, and_36_out, and_37_out, and_38_out, and_39_out, and_40_out, and_41_out,
       and_42_out, and_43_out, and_44_out, and_45_out, and_46_out, and_47_out, and_48_out, and_49_out,
       and_50_out, and_51_out, and_52_out, and_53_out, and_54_out, and_55_out, and_56_out, and_57_out,
       and_58_out, and_59_out, and_60_out, and_61_out, and_62_out, and_63_out, and_64_out, and_65_out,
       and_66_out, and_67_out, and_68_out, and_69_out, and_70_out, and_71_out, and_72_out, and_73_out,
       and_74_out, and_75_out, and_76_out, and_77_out, and_78_out, and_79_out, and_80_out, and_81_out,
       and_82_out, and_83_out, and_84_out, and_85_out, and_86_out, and_87_out, and_88_out, and_89_out,
       and_90_out, and_91_out, and_92_out, and_93_out, and_94_out, and_95_out, and_96_out, and_97_out,
       and_98_out, and_99_out, and_100_out, and_101_out, and_102_out, and_103_out, and_104_out, and_105_out,
       and_106_out, and_107_out, and_108_out, and_109_out, and_110_out, and_111_out, and_112_out,
       and_113_out, and_114_out, and_115_out, and_116_out, and_117_out, and_118_out, and_119_out,
       and_120_out, and_121_out, and_122_out, and_123_out, and_124_out, and_125_out, and_126_out,
       and_127_out, and_128_out, and_129_out, and_130_out, and_131_out, and_132_out, and_133_out,
       and_134_out, and_135_out, and_136_out, controlled_buffer_8_out, controlled_buffer_16_out,
       controlled_buffer_24_out, controlled_buffer_32_out, controlled_buffer_40_out,
       controlled_buffer_48_out, controlled_buffer_56_out, d_ff_1_q, d_ff_2_q, d_ff_3_q, d_ff_4_q, d_ff_5_q,
       d_ff_6_q, d_ff_7_q, d_ff_8_q, d_ff_9_q, d_ff_10_q, d_ff_11_q, d_ff_12_q, d_ff_13_q, d_ff_14_q,
       d_ff_15_q, d_ff_16_q, d_ff_17_q, d_ff_18_q, d_ff_19_q, d_ff_20_q, d_ff_21_q, d_ff_22_q, d_ff_23_q,
       d_ff_24_q, d_ff_25_q, d_ff_26_q, d_ff_27_q, d_ff_28_q, d_ff_29_q, d_ff_30_q, d_ff_31_q, d_ff_32_q,
       d_ff_33_q, d_ff_34_q, d_ff_35_q, d_ff_36_q, d_ff_37_q, d_ff_38_q, d_ff_39_q, d_ff_40_q, d_ff_41_q,
       d_ff_42_q, d_ff_43_q, d_ff_44_q, d_ff_45_q, d_ff_46_q, d_ff_47_q, d_ff_48_q, d_ff_49_q, d_ff_50_q,
       d_ff_51_q, d_ff_52_q, d_ff_53_q, d_ff_54_q, d_ff_55_q, d_ff_56_q, d_ff_57_q, d_ff_58_q, d_ff_59_q,
       d_ff_60_q, d_ff_61_q, d_ff_62_q, d_ff_63_q, D_Flip_Flop_q, not_1_out, not_2_out, not_3_out, not_4_out,
       not_5_out, not_6_out, not_7_out, not_8_out, not_9_out, not_10_out, not_11_out, not_12_out, not_13_out,
       not_14_out, not_15_out, not_16_out, not_17_out, not_18_out, not_19_out, not_20_out, not_21_out,
       not_22_out, not_23_out, not_24_out, not_25_out, not_26_out, not_27_out, not_28_out, not_29_out,
       not_30_out, not_31_out, not_32_out, not_33_out, not_34_out, not_35_out, not_36_out, not_37_out,
       not_38_out, not_39_out, not_40_out, not_41_out, not_42_out, not_43_out, not_44_out, not_45_out,
       not_46_out, not_47_out, not_48_out, not_49_out, not_50_out, not_51_out, not_52_out, not_53_out,
       not_54_out, not_55_out, not_56_out, not_57_out, not_58_out, not_59_out, not_60_out, not_61_out,
       not_62_out, not_63_out, not_64_out, not_65_out, not_66_out, not_67_out, or_1_out, or_2_out, or_3_out,
       or_4_out, or_5_out, or_6_out, or_7_out, or_8_out, or_9_out, or_10_out, or_11_out, or_12_out,
       or_13_out, or_14_out, or_15_out, or_16_out, or_17_out, or_18_out, or_19_out, or_20_out, or_21_out,
       or_22_out, or_23_out, or_24_out, or_25_out, or_26_out, or_27_out, or_28_out, or_29_out, or_30_out,
       or_31_out, or_32_out, or_33_out, or_34_out, or_35_out, or_36_out, or_37_out, or_38_out, or_39_out,
       or_40_out, or_41_out, or_42_out, or_43_out, or_44_out, or_45_out, or_46_out, or_47_out, or_48_out,
       or_49_out, or_50_out, or_51_out, or_52_out, or_53_out, or_54_out, or_55_out, or_56_out, or_57_out,
       or_58_out, or_59_out, or_60_out, or_61_out, or_62_out, or_63_out, or_64_out, tri_state_logic_out;

  not not_1 (not_1_out, A0);
  not not_2 (not_2_out, A1);
  not not_3 (not_3_out, A2);
  and and_1 (and_1_out, not_1_out, not_2_out, not_3_out, EN);
  and and_2 (and_2_out, A0, not_2_out, not_3_out, EN);
  and and_3 (and_3_out, not_1_out, A1, not_3_out, EN);
  and and_4 (and_4_out, A0, A1, not_3_out, EN);
  and and_5 (and_5_out, not_1_out, not_2_out, A2, EN);
  and and_6 (and_6_out, A0, not_2_out, A2, EN);
  and and_7 (and_7_out, not_1_out, A1, A2, EN);
  and and_8 (and_8_out, A0, A1, A2, EN);
  not not_4 (not_4_out, and_1_out);
  not not_5 (not_5_out, and_2_out);
  not not_6 (not_6_out, and_3_out);
  not not_7 (not_7_out, and_4_out);
  not not_8 (not_8_out, and_5_out);
  not not_9 (not_9_out, and_6_out);
  not not_10 (not_10_out, and_7_out);
  not not_11 (not_11_out, and_8_out);
  and and_9 (and_9_out, D_Flip_Flop_q, not_4_out);
  and and_10 (and_10_out, and_1_out, Data);
  and and_11 (and_11_out, d_ff_1_q, not_5_out);
  and and_12 (and_12_out, and_2_out, Data);
  and and_13 (and_13_out, d_ff_2_q, not_6_out);
  and and_14 (and_14_out, and_3_out, Data);
  and and_15 (and_15_out, d_ff_3_q, not_7_out);
  and and_16 (and_16_out, and_4_out, Data);
  and and_17 (and_17_out, d_ff_4_q, not_8_out);
  and and_18 (and_18_out, and_5_out, Data);
  and and_19 (and_19_out, d_ff_5_q, not_9_out);
  and and_20 (and_20_out, and_6_out, Data);
  and and_21 (and_21_out, d_ff_6_q, not_10_out);
  and and_22 (and_22_out, and_7_out, Data);
  and and_23 (and_23_out, d_ff_7_q, not_11_out);
  and and_24 (and_24_out, and_8_out, Data);
  or or_1 (or_1_out, and_9_out, and_10_out);
  or or_2 (or_2_out, and_11_out, and_12_out);
  or or_3 (or_3_out, and_13_out, and_14_out);
  or or_4 (or_4_out, and_15_out, and_16_out);
  or or_5 (or_5_out, and_17_out, and_18_out);
  or or_6 (or_6_out, and_19_out, and_20_out);
  or or_7 (or_7_out, and_21_out, and_22_out);
  or or_8 (or_8_out, and_23_out, and_24_out);
  D_Flip_Flop D_Flip_Flop (.D(or_1_out), .clk(Clock), .Q(D_Flip_Flop_q));  // open: Qn, preset, reset
  D_Flip_Flop d_ff_1 (.D(or_2_out), .clk(Clock), .Q(d_ff_1_q));  // open: Qn, preset, reset
  D_Flip_Flop d_ff_2 (.D(or_3_out), .clk(Clock), .Q(d_ff_2_q));  // open: Qn, preset, reset
  D_Flip_Flop d_ff_3 (.D(or_4_out), .clk(Clock), .Q(d_ff_3_q));  // open: Qn, preset, reset
  D_Flip_Flop d_ff_4 (.D(or_5_out), .clk(Clock), .Q(d_ff_4_q));  // open: Qn, preset, reset
  D_Flip_Flop d_ff_5 (.D(or_6_out), .clk(Clock), .Q(d_ff_5_q));  // open: Qn, preset, reset
  D_Flip_Flop d_ff_6 (.D(or_7_out), .clk(Clock), .Q(d_ff_6_q));  // open: Qn, preset, reset
  D_Flip_Flop d_ff_7 (.D(or_8_out), .clk(Clock), .Q(d_ff_7_q));  // open: Qn, preset, reset
  assign tri_state_logic_out = Output_Ctrl ? D_Flip_Flop_q : 1'bz;  // Controlled_Buffer tri_state_logic
  LED led_1 (.in(D_Flip_Flop_q));
  assign tri_state_logic_out = Output_Ctrl_2 ? d_ff_1_q : 1'bz;  // Controlled_Buffer controlled_buffer_1
  LED led_2 (.in(d_ff_1_q));
  assign tri_state_logic_out = Output_Ctrl_3 ? d_ff_2_q : 1'bz;  // Controlled_Buffer controlled_buffer_2
  LED led_3 (.in(d_ff_2_q));
  assign tri_state_logic_out = Output_Ctrl_4 ? d_ff_3_q : 1'bz;  // Controlled_Buffer controlled_buffer_3
  LED led_4 (.in(d_ff_3_q));
  assign tri_state_logic_out = Output_Ctrl_5 ? d_ff_4_q : 1'bz;  // Controlled_Buffer controlled_buffer_4
  LED led_5 (.in(d_ff_4_q));
  assign tri_state_logic_out = Output_Ctrl_6 ? d_ff_5_q : 1'bz;  // Controlled_Buffer controlled_buffer_5
  LED led_6 (.in(d_ff_5_q));
  assign tri_state_logic_out = Output_Ctrl_7 ? d_ff_6_q : 1'bz;  // Controlled_Buffer controlled_buffer_6
  LED led_7 (.in(d_ff_6_q));
  assign tri_state_logic_out = Output_Ctrl_8 ? d_ff_7_q : 1'bz;  // Controlled_Buffer controlled_buffer_7
  LED led_8 (.in(d_ff_7_q));
  LED led_9 (.in(tri_state_logic_out));
  and and_25 (and_25_out, d_ff_8_q, not_12_out);
  not not_12 (not_12_out, and_1_out);
  and and_26 (and_26_out, and_1_out, in_1);
  and and_27 (and_27_out, d_ff_9_q, not_13_out);
  not not_13 (not_13_out, and_2_out);
  and and_28 (and_28_out, and_2_out, in_1);
  and and_29 (and_29_out, d_ff_10_q, not_14_out);
  not not_14 (not_14_out, and_3_out);
  and and_30 (and_30_out, and_3_out, in_1);
  and and_31 (and_31_out, d_ff_11_q, not_15_out);
  not not_15 (not_15_out, and_4_out);
  and and_32 (and_32_out, and_4_out, in_1);
  and and_33 (and_33_out, d_ff_12_q, not_16_out);
  not not_16 (not_16_out, and_5_out);
  and and_34 (and_34_out, and_5_out, in_1);
  and and_35 (and_35_out, d_ff_13_q, not_17_out);
  not not_17 (not_17_out, and_6_out);
  and and_36 (and_36_out, and_6_out, in_1);
  and and_37 (and_37_out, d_ff_14_q, not_18_out);
  not not_18 (not_18_out, and_7_out);
  and and_38 (and_38_out, and_7_out, in_1);
  and and_39 (and_39_out, d_ff_15_q, not_19_out);
  not not_19 (not_19_out, and_8_out);
  and and_40 (and_40_out, and_8_out, in_1);
  or or_9 (or_9_out, and_25_out, and_26_out);
  or or_10 (or_10_out, and_27_out, and_28_out);
  or or_11 (or_11_out, and_29_out, and_30_out);
  or or_12 (or_12_out, and_31_out, and_32_out);
  or or_13 (or_13_out, and_33_out, and_34_out);
  or or_14 (or_14_out, and_35_out, and_36_out);
  or or_15 (or_15_out, and_37_out, and_38_out);
  or or_16 (or_16_out, and_39_out, and_40_out);
  D_Flip_Flop d_ff_8 (.D(or_9_out), .clk(Clock), .Q(d_ff_8_q));  // open: Qn, preset, reset
  D_Flip_Flop d_ff_9 (.D(or_10_out), .clk(Clock), .Q(d_ff_9_q));  // open: Qn, preset, reset
  D_Flip_Flop d_ff_10 (.D(or_11_out), .clk(Clock), .Q(d_ff_10_q));  // open: Qn, preset, reset
  D_Flip_Flop d_ff_11 (.D(or_12_out), .clk(Clock), .Q(d_ff_11_q));  // open: Qn, preset, reset
  D_Flip_Flop d_ff_12 (.D(or_13_out), .clk(Clock), .Q(d_ff_12_q));  // open: Qn, preset, reset
  D_Flip_Flop d_ff_13 (.D(or_14_out), .clk(Clock), .Q(d_ff_13_q));  // open: Qn, preset, reset
  D_Flip_Flop d_ff_14 (.D(or_15_out), .clk(Clock), .Q(d_ff_14_q));  // open: Qn, preset, reset
  D_Flip_Flop d_ff_15 (.D(or_16_out), .clk(Clock), .Q(d_ff_15_q));  // open: Qn, preset, reset
  assign controlled_buffer_8_out = Output_Ctrl ? d_ff_8_q : 1'bz;  // Controlled_Buffer controlled_buffer_8
  assign controlled_buffer_8_out = Output_Ctrl_2 ? d_ff_9_q : 1'bz;  // Controlled_Buffer controlled_buffer_9
  assign controlled_buffer_8_out = Output_Ctrl_3 ? d_ff_10_q : 1'bz;  // Controlled_Buffer controlled_buffer_10
  assign controlled_buffer_8_out = Output_Ctrl_4 ? d_ff_11_q : 1'bz;  // Controlled_Buffer controlled_buffer_11
  assign controlled_buffer_8_out = Output_Ctrl_5 ? d_ff_12_q : 1'bz;  // Controlled_Buffer controlled_buffer_12
  assign controlled_buffer_8_out = Output_Ctrl_6 ? d_ff_13_q : 1'bz;  // Controlled_Buffer controlled_buffer_13
  assign controlled_buffer_8_out = Output_Ctrl_7 ? d_ff_14_q : 1'bz;  // Controlled_Buffer controlled_buffer_14
  assign controlled_buffer_8_out = Output_Ctrl_8 ? d_ff_15_q : 1'bz;  // Controlled_Buffer controlled_buffer_15
  LED led_10 (.in(d_ff_8_q));
  LED led_11 (.in(d_ff_9_q));
  LED led_12 (.in(d_ff_10_q));
  LED led_13 (.in(d_ff_11_q));
  LED led_14 (.in(d_ff_12_q));
  LED led_15 (.in(d_ff_13_q));
  LED led_16 (.in(d_ff_14_q));
  LED led_17 (.in(d_ff_15_q));
  LED led_18 (.in(controlled_buffer_8_out));
  not not_20 (not_20_out, and_1_out);
  not not_21 (not_21_out, and_2_out);
  not not_22 (not_22_out, and_3_out);
  not not_23 (not_23_out, and_4_out);
  not not_24 (not_24_out, and_5_out);
  not not_25 (not_25_out, and_6_out);
  not not_26 (not_26_out, and_7_out);
  not not_27 (not_27_out, and_8_out);
  and and_41 (and_41_out, d_ff_16_q, not_20_out);
  and and_42 (and_42_out, and_1_out, in_4);
  and and_43 (and_43_out, d_ff_17_q, not_21_out);
  and and_44 (and_44_out, and_2_out, in_4);
  and and_45 (and_45_out, d_ff_18_q, not_22_out);
  and and_46 (and_46_out, and_3_out, in_4);
  and and_47 (and_47_out, d_ff_19_q, not_23_out);
  and and_48 (and_48_out, and_4_out, in_4);
  and and_49 (and_49_out, d_ff_20_q, not_24_out);
  and and_50 (and_50_out, and_5_out, in_4);
  and and_51 (and_51_out, d_ff_21_q, not_25_out);
  and and_52 (and_52_out, and_6_out, in_4);
  and and_53 (and_53_out, d_ff_22_q, not_26_out);
  and and_54 (and_54_out, and_7_out, in_4);
  and and_55 (and_55_out, d_ff_23_q, not_27_out);
  and and_56 (and_56_out, and_8_out, in_4);
  or or_17 (or_17_out, and_41_out, and_42_out);
  or or_18 (or_18_out, and_43_out, and_44_out);
  or or_19 (or_19_out, and_45_out, and_46_out);
  or or_20 (or_20_out, and_47_out, and_48_out);
  or or_21 (or_21_out, and_49_out, and_50_out);
  or or_22 (or_22_out, and_51_out, and_52_out);
  or or_23 (or_23_out, and_53_out, and_54_out);
  or or_24 (or_24_out, and_55_out, and_56_out);
  D_Flip_Flop d_ff_16 (.D(or_17_out), .clk(Clock), .Q(d_ff_16_q));  // open: Qn, preset, reset
  D_Flip_Flop d_ff_17 (.D(or_18_out), .clk(Clock), .Q(d_ff_17_q));  // open: Qn, preset, reset
  D_Flip_Flop d_ff_18 (.D(or_19_out), .clk(Clock), .Q(d_ff_18_q));  // open: Qn, preset, reset
  D_Flip_Flop d_ff_19 (.D(or_20_out), .clk(Clock), .Q(d_ff_19_q));  // open: Qn, preset, reset
  D_Flip_Flop d_ff_20 (.D(or_21_out), .clk(Clock), .Q(d_ff_20_q));  // open: Qn, preset, reset
  D_Flip_Flop d_ff_21 (.D(or_22_out), .clk(Clock), .Q(d_ff_21_q));  // open: Qn, preset, reset
  D_Flip_Flop d_ff_22 (.D(or_23_out), .clk(Clock), .Q(d_ff_22_q));  // open: Qn, preset, reset
  D_Flip_Flop d_ff_23 (.D(or_24_out), .clk(Clock), .Q(d_ff_23_q));  // open: Qn, preset, reset
  assign controlled_buffer_16_out = Output_Ctrl ? d_ff_16_q : 1'bz;  // Controlled_Buffer controlled_buffer_16
  assign controlled_buffer_16_out = Output_Ctrl_2 ? d_ff_17_q : 1'bz;  // Controlled_Buffer controlled_buffer_17
  assign controlled_buffer_16_out = Output_Ctrl_3 ? d_ff_18_q : 1'bz;  // Controlled_Buffer controlled_buffer_18
  assign controlled_buffer_16_out = Output_Ctrl_4 ? d_ff_19_q : 1'bz;  // Controlled_Buffer controlled_buffer_19
  assign controlled_buffer_16_out = Output_Ctrl_5 ? d_ff_20_q : 1'bz;  // Controlled_Buffer controlled_buffer_20
  assign controlled_buffer_16_out = Output_Ctrl_6 ? d_ff_21_q : 1'bz;  // Controlled_Buffer controlled_buffer_21
  assign controlled_buffer_16_out = Output_Ctrl_7 ? d_ff_22_q : 1'bz;  // Controlled_Buffer controlled_buffer_22
  assign controlled_buffer_16_out = Output_Ctrl_8 ? d_ff_23_q : 1'bz;  // Controlled_Buffer controlled_buffer_23
  LED led_19 (.in(d_ff_16_q));
  LED led_20 (.in(d_ff_17_q));
  LED led_21 (.in(d_ff_18_q));
  LED led_22 (.in(d_ff_19_q));
  LED led_23 (.in(d_ff_20_q));
  LED led_24 (.in(d_ff_21_q));
  LED led_25 (.in(d_ff_22_q));
  LED led_26 (.in(d_ff_23_q));
  LED led_27 (.in(controlled_buffer_16_out));
  not not_28 (not_28_out, and_1_out);
  not not_29 (not_29_out, and_2_out);
  not not_30 (not_30_out, and_3_out);
  not not_31 (not_31_out, and_4_out);
  not not_32 (not_32_out, and_5_out);
  not not_33 (not_33_out, and_6_out);
  not not_34 (not_34_out, and_7_out);
  not not_35 (not_35_out, and_8_out);
  and and_57 (and_57_out, d_ff_24_q, not_28_out);
  and and_58 (and_58_out, and_1_out, in_6);
  and and_59 (and_59_out, d_ff_25_q, not_29_out);
  and and_60 (and_60_out, and_2_out, in_6);
  and and_61 (and_61_out, d_ff_26_q, not_30_out);
  and and_62 (and_62_out, and_3_out, in_6);
  and and_63 (and_63_out, d_ff_27_q, not_31_out);
  and and_64 (and_64_out, and_4_out, in_6);
  and and_65 (and_65_out, d_ff_28_q, not_32_out);
  and and_66 (and_66_out, and_5_out, in_6);
  and and_67 (and_67_out, d_ff_29_q, not_33_out);
  and and_68 (and_68_out, and_6_out, in_6);
  and and_69 (and_69_out, d_ff_30_q, not_34_out);
  and and_70 (and_70_out, and_7_out, in_6);
  and and_71 (and_71_out, d_ff_31_q, not_35_out);
  and and_72 (and_72_out, and_8_out, in_6);
  D_Flip_Flop d_ff_24 (.D(or_25_out), .clk(Clock), .Q(d_ff_24_q));  // open: Qn, preset, reset
  or or_25 (or_25_out, and_57_out, and_58_out);
  D_Flip_Flop d_ff_25 (.D(or_26_out), .clk(Clock), .Q(d_ff_25_q));  // open: Qn, preset, reset
  or or_26 (or_26_out, and_59_out, and_60_out);
  D_Flip_Flop d_ff_26 (.D(or_27_out), .clk(Clock), .Q(d_ff_26_q));  // open: Qn, preset, reset
  or or_27 (or_27_out, and_61_out, and_62_out);
  D_Flip_Flop d_ff_27 (.D(or_28_out), .clk(Clock), .Q(d_ff_27_q));  // open: Qn, preset, reset
  or or_28 (or_28_out, and_63_out, and_64_out);
  D_Flip_Flop d_ff_28 (.D(or_29_out), .clk(Clock), .Q(d_ff_28_q));  // open: Qn, preset, reset
  or or_29 (or_29_out, and_65_out, and_66_out);
  D_Flip_Flop d_ff_29 (.D(or_30_out), .clk(Clock), .Q(d_ff_29_q));  // open: Qn, preset, reset
  or or_30 (or_30_out, and_67_out, and_68_out);
  D_Flip_Flop d_ff_30 (.D(or_31_out), .clk(Clock), .Q(d_ff_30_q));  // open: Qn, preset, reset
  or or_31 (or_31_out, and_69_out, and_70_out);
  D_Flip_Flop d_ff_31 (.D(or_32_out), .clk(Clock), .Q(d_ff_31_q));  // open: Qn, preset, reset
  or or_32 (or_32_out, and_71_out, and_72_out);
  assign controlled_buffer_24_out = Output_Ctrl ? d_ff_24_q : 1'bz;  // Controlled_Buffer controlled_buffer_24
  LED led_28 (.in(d_ff_24_q));
  assign controlled_buffer_24_out = Output_Ctrl_2 ? d_ff_25_q : 1'bz;  // Controlled_Buffer controlled_buffer_25
  LED led_29 (.in(d_ff_25_q));
  assign controlled_buffer_24_out = Output_Ctrl_3 ? d_ff_26_q : 1'bz;  // Controlled_Buffer controlled_buffer_26
  LED led_30 (.in(d_ff_26_q));
  assign controlled_buffer_24_out = Output_Ctrl_4 ? d_ff_27_q : 1'bz;  // Controlled_Buffer controlled_buffer_27
  LED led_31 (.in(d_ff_27_q));
  assign controlled_buffer_24_out = Output_Ctrl_5 ? d_ff_28_q : 1'bz;  // Controlled_Buffer controlled_buffer_28
  LED led_32 (.in(d_ff_28_q));
  assign controlled_buffer_24_out = Output_Ctrl_6 ? d_ff_29_q : 1'bz;  // Controlled_Buffer controlled_buffer_29
  LED led_33 (.in(d_ff_29_q));
  assign controlled_buffer_24_out = Output_Ctrl_7 ? d_ff_30_q : 1'bz;  // Controlled_Buffer controlled_buffer_30
  LED led_34 (.in(d_ff_30_q));
  assign controlled_buffer_24_out = Output_Ctrl_8 ? d_ff_31_q : 1'bz;  // Controlled_Buffer controlled_buffer_31
  LED led_35 (.in(d_ff_31_q));
  LED led_36 (.in(controlled_buffer_24_out));
  not not_36 (not_36_out, and_1_out);
  not not_37 (not_37_out, and_2_out);
  not not_38 (not_38_out, and_3_out);
  not not_39 (not_39_out, and_4_out);
  not not_40 (not_40_out, and_5_out);
  not not_41 (not_41_out, and_6_out);
  not not_42 (not_42_out, and_7_out);
  not not_43 (not_43_out, and_8_out);
  and and_73 (and_73_out, d_ff_32_q, not_36_out);
  and and_74 (and_74_out, and_1_out, in_5);
  and and_75 (and_75_out, d_ff_33_q, not_37_out);
  and and_76 (and_76_out, and_2_out, in_5);
  and and_77 (and_77_out, d_ff_34_q, not_38_out);
  and and_78 (and_78_out, and_3_out, in_5);
  and and_79 (and_79_out, d_ff_35_q, not_39_out);
  and and_80 (and_80_out, and_4_out, in_5);
  and and_81 (and_81_out, d_ff_36_q, not_40_out);
  and and_82 (and_82_out, and_5_out, in_5);
  and and_83 (and_83_out, d_ff_37_q, not_41_out);
  and and_84 (and_84_out, and_6_out, in_5);
  and and_85 (and_85_out, d_ff_38_q, not_42_out);
  and and_86 (and_86_out, and_7_out, in_5);
  and and_87 (and_87_out, d_ff_39_q, not_43_out);
  and and_88 (and_88_out, and_8_out, in_5);
  or or_33 (or_33_out, and_73_out, and_74_out);
  or or_34 (or_34_out, and_75_out, and_76_out);
  or or_35 (or_35_out, and_77_out, and_78_out);
  or or_36 (or_36_out, and_79_out, and_80_out);
  or or_37 (or_37_out, and_81_out, and_82_out);
  or or_38 (or_38_out, and_83_out, and_84_out);
  or or_39 (or_39_out, and_85_out, and_86_out);
  or or_40 (or_40_out, and_87_out, and_88_out);
  D_Flip_Flop d_ff_32 (.D(or_33_out), .clk(Clock), .Q(d_ff_32_q));  // open: Qn, preset, reset
  D_Flip_Flop d_ff_33 (.D(or_34_out), .clk(Clock), .Q(d_ff_33_q));  // open: Qn, preset, reset
  D_Flip_Flop d_ff_34 (.D(or_35_out), .clk(Clock), .Q(d_ff_34_q));  // open: Qn, preset, reset
  D_Flip_Flop d_ff_35 (.D(or_36_out), .clk(Clock), .Q(d_ff_35_q));  // open: Qn, preset, reset
  D_Flip_Flop d_ff_36 (.D(or_37_out), .clk(Clock), .Q(d_ff_36_q));  // open: Qn, preset, reset
  D_Flip_Flop d_ff_37 (.D(or_38_out), .clk(Clock), .Q(d_ff_37_q));  // open: Qn, preset, reset
  D_Flip_Flop d_ff_38 (.D(or_39_out), .clk(Clock), .Q(d_ff_38_q));  // open: Qn, preset, reset
  D_Flip_Flop d_ff_39 (.D(or_40_out), .clk(Clock), .Q(d_ff_39_q));  // open: Qn, preset, reset
  assign controlled_buffer_32_out = Output_Ctrl ? d_ff_32_q : 1'bz;  // Controlled_Buffer controlled_buffer_32
  LED led_37 (.in(d_ff_32_q));
  assign controlled_buffer_32_out = Output_Ctrl_2 ? d_ff_33_q : 1'bz;  // Controlled_Buffer controlled_buffer_33
  LED led_38 (.in(d_ff_33_q));
  assign controlled_buffer_32_out = Output_Ctrl_3 ? d_ff_34_q : 1'bz;  // Controlled_Buffer controlled_buffer_34
  LED led_39 (.in(d_ff_34_q));
  assign controlled_buffer_32_out = Output_Ctrl_4 ? d_ff_35_q : 1'bz;  // Controlled_Buffer controlled_buffer_35
  LED led_40 (.in(d_ff_35_q));
  assign controlled_buffer_32_out = Output_Ctrl_5 ? d_ff_36_q : 1'bz;  // Controlled_Buffer controlled_buffer_36
  LED led_41 (.in(d_ff_36_q));
  assign controlled_buffer_32_out = Output_Ctrl_6 ? d_ff_37_q : 1'bz;  // Controlled_Buffer controlled_buffer_37
  LED led_42 (.in(d_ff_37_q));
  assign controlled_buffer_32_out = Output_Ctrl_7 ? d_ff_38_q : 1'bz;  // Controlled_Buffer controlled_buffer_38
  LED led_43 (.in(d_ff_38_q));
  assign controlled_buffer_32_out = Output_Ctrl_8 ? d_ff_39_q : 1'bz;  // Controlled_Buffer controlled_buffer_39
  LED led_44 (.in(d_ff_39_q));
  LED led_45 (.in(controlled_buffer_32_out));
  and and_89 (and_89_out, d_ff_40_q, not_44_out);
  not not_44 (not_44_out, and_1_out);
  and and_90 (and_90_out, and_1_out, in_2);
  and and_91 (and_91_out, d_ff_41_q, not_45_out);
  not not_45 (not_45_out, and_2_out);
  and and_92 (and_92_out, and_2_out, in_2);
  and and_93 (and_93_out, d_ff_42_q, not_46_out);
  not not_46 (not_46_out, and_3_out);
  and and_94 (and_94_out, and_3_out, in_2);
  and and_95 (and_95_out, d_ff_43_q, not_47_out);
  not not_47 (not_47_out, and_4_out);
  and and_96 (and_96_out, and_4_out, in_2);
  and and_97 (and_97_out, d_ff_44_q, not_48_out);
  not not_48 (not_48_out, and_5_out);
  and and_98 (and_98_out, and_5_out, in_2);
  and and_99 (and_99_out, d_ff_45_q, not_49_out);
  not not_49 (not_49_out, and_6_out);
  and and_100 (and_100_out, and_6_out, in_2);
  and and_101 (and_101_out, d_ff_46_q, not_50_out);
  not not_50 (not_50_out, and_7_out);
  and and_102 (and_102_out, and_7_out, in_2);
  and and_103 (and_103_out, d_ff_47_q, not_51_out);
  not not_51 (not_51_out, and_8_out);
  and and_104 (and_104_out, and_8_out, in_2);
  or or_41 (or_41_out, and_89_out, and_90_out);
  or or_42 (or_42_out, and_91_out, and_92_out);
  or or_43 (or_43_out, and_93_out, and_94_out);
  or or_44 (or_44_out, and_95_out, and_96_out);
  or or_45 (or_45_out, and_97_out, and_98_out);
  or or_46 (or_46_out, and_99_out, and_100_out);
  or or_47 (or_47_out, and_101_out, and_102_out);
  or or_48 (or_48_out, and_103_out, and_104_out);
  D_Flip_Flop d_ff_40 (.D(or_41_out), .clk(Clock), .Q(d_ff_40_q));  // open: Qn, preset, reset
  D_Flip_Flop d_ff_41 (.D(or_42_out), .clk(Clock), .Q(d_ff_41_q));  // open: Qn, preset, reset
  D_Flip_Flop d_ff_42 (.D(or_43_out), .clk(Clock), .Q(d_ff_42_q));  // open: Qn, preset, reset
  D_Flip_Flop d_ff_43 (.D(or_44_out), .clk(Clock), .Q(d_ff_43_q));  // open: Qn, preset, reset
  D_Flip_Flop d_ff_44 (.D(or_45_out), .clk(Clock), .Q(d_ff_44_q));  // open: Qn, preset, reset
  D_Flip_Flop d_ff_45 (.D(or_46_out), .clk(Clock), .Q(d_ff_45_q));  // open: Qn, preset, reset
  D_Flip_Flop d_ff_46 (.D(or_47_out), .clk(Clock), .Q(d_ff_46_q));  // open: Qn, preset, reset
  D_Flip_Flop d_ff_47 (.D(or_48_out), .clk(Clock), .Q(d_ff_47_q));  // open: Qn, preset, reset
  assign controlled_buffer_40_out = Output_Ctrl ? d_ff_40_q : 1'bz;  // Controlled_Buffer controlled_buffer_40
  assign controlled_buffer_40_out = Output_Ctrl_2 ? d_ff_41_q : 1'bz;  // Controlled_Buffer controlled_buffer_41
  assign controlled_buffer_40_out = Output_Ctrl_3 ? d_ff_42_q : 1'bz;  // Controlled_Buffer controlled_buffer_42
  assign controlled_buffer_40_out = Output_Ctrl_4 ? d_ff_43_q : 1'bz;  // Controlled_Buffer controlled_buffer_43
  assign controlled_buffer_40_out = Output_Ctrl_5 ? d_ff_44_q : 1'bz;  // Controlled_Buffer controlled_buffer_44
  assign controlled_buffer_40_out = Output_Ctrl_6 ? d_ff_45_q : 1'bz;  // Controlled_Buffer controlled_buffer_45
  assign controlled_buffer_40_out = Output_Ctrl_7 ? d_ff_46_q : 1'bz;  // Controlled_Buffer controlled_buffer_46
  assign controlled_buffer_40_out = Output_Ctrl_8 ? d_ff_47_q : 1'bz;  // Controlled_Buffer controlled_buffer_47
  LED led_46 (.in(d_ff_40_q));
  LED led_47 (.in(d_ff_41_q));
  LED led_48 (.in(d_ff_42_q));
  LED led_49 (.in(d_ff_43_q));
  LED led_50 (.in(d_ff_44_q));
  LED led_51 (.in(d_ff_45_q));
  LED led_52 (.in(d_ff_46_q));
  LED led_53 (.in(d_ff_47_q));
  LED led_54 (.in(controlled_buffer_40_out));
  not not_52 (not_52_out, and_1_out);
  not not_53 (not_53_out, and_2_out);
  not not_54 (not_54_out, and_3_out);
  not not_55 (not_55_out, and_4_out);
  not not_56 (not_56_out, and_5_out);
  not not_57 (not_57_out, and_6_out);
  not not_58 (not_58_out, and_7_out);
  not not_59 (not_59_out, and_8_out);
  and and_105 (and_105_out, d_ff_48_q, not_52_out);
  and and_106 (and_106_out, and_1_out, in_7);
  and and_107 (and_107_out, d_ff_49_q, not_53_out);
  and and_108 (and_108_out, and_2_out, in_7);
  and and_109 (and_109_out, d_ff_50_q, not_54_out);
  and and_110 (and_110_out, and_3_out, in_7);
  and and_111 (and_111_out, d_ff_51_q, not_55_out);
  and and_112 (and_112_out, and_4_out, in_7);
  and and_113 (and_113_out, d_ff_52_q, not_56_out);
  and and_114 (and_114_out, and_5_out, in_7);
  and and_115 (and_115_out, d_ff_53_q, not_57_out);
  and and_116 (and_116_out, and_6_out, in_7);
  and and_117 (and_117_out, d_ff_54_q, not_58_out);
  and and_118 (and_118_out, and_7_out, in_7);
  and and_119 (and_119_out, d_ff_55_q, not_59_out);
  and and_120 (and_120_out, and_8_out, in_7);
  or or_49 (or_49_out, and_105_out, and_106_out);
  or or_50 (or_50_out, and_107_out, and_108_out);
  or or_51 (or_51_out, and_109_out, and_110_out);
  or or_52 (or_52_out, and_111_out, and_112_out);
  or or_53 (or_53_out, and_113_out, and_114_out);
  or or_54 (or_54_out, and_115_out, and_116_out);
  or or_55 (or_55_out, and_117_out, and_118_out);
  or or_56 (or_56_out, and_119_out, and_120_out);
  D_Flip_Flop d_ff_48 (.D(or_49_out), .clk(Clock), .Q(d_ff_48_q));  // open: Qn, preset, reset
  D_Flip_Flop d_ff_49 (.D(or_50_out), .clk(Clock), .Q(d_ff_49_q));  // open: Qn, preset, reset
  D_Flip_Flop d_ff_50 (.D(or_51_out), .clk(Clock), .Q(d_ff_50_q));  // open: Qn, preset, reset
  D_Flip_Flop d_ff_51 (.D(or_52_out), .clk(Clock), .Q(d_ff_51_q));  // open: Qn, preset, reset
  D_Flip_Flop d_ff_52 (.D(or_53_out), .clk(Clock), .Q(d_ff_52_q));  // open: Qn, preset, reset
  D_Flip_Flop d_ff_53 (.D(or_54_out), .clk(Clock), .Q(d_ff_53_q));  // open: Qn, preset, reset
  D_Flip_Flop d_ff_54 (.D(or_55_out), .clk(Clock), .Q(d_ff_54_q));  // open: Qn, preset, reset
  D_Flip_Flop d_ff_55 (.D(or_56_out), .clk(Clock), .Q(d_ff_55_q));  // open: Qn, preset, reset
  assign controlled_buffer_48_out = Output_Ctrl ? d_ff_48_q : 1'bz;  // Controlled_Buffer controlled_buffer_48
  assign controlled_buffer_48_out = Output_Ctrl_2 ? d_ff_49_q : 1'bz;  // Controlled_Buffer controlled_buffer_49
  assign controlled_buffer_48_out = Output_Ctrl_3 ? d_ff_50_q : 1'bz;  // Controlled_Buffer controlled_buffer_50
  assign controlled_buffer_48_out = Output_Ctrl_4 ? d_ff_51_q : 1'bz;  // Controlled_Buffer controlled_buffer_51
  assign controlled_buffer_48_out = Output_Ctrl_5 ? d_ff_52_q : 1'bz;  // Controlled_Buffer controlled_buffer_52
  assign controlled_buffer_48_out = Output_Ctrl_6 ? d_ff_53_q : 1'bz;  // Controlled_Buffer controlled_buffer_53
  assign controlled_buffer_48_out = Output_Ctrl_7 ? d_ff_54_q : 1'bz;  // Controlled_Buffer controlled_buffer_54
  assign controlled_buffer_48_out = Output_Ctrl_8 ? d_ff_55_q : 1'bz;  // Controlled_Buffer controlled_buffer_55
  LED led_55 (.in(d_ff_48_q));
  LED led_56 (.in(d_ff_49_q));
  LED led_57 (.in(d_ff_50_q));
  LED led_58 (.in(d_ff_51_q));
  LED led_59 (.in(d_ff_52_q));
  LED led_60 (.in(d_ff_53_q));
  LED led_61 (.in(d_ff_54_q));
  LED led_62 (.in(d_ff_55_q));
  LED led_63 (.in(controlled_buffer_48_out));
  not not_60 (not_60_out, and_1_out);
  not not_61 (not_61_out, and_2_out);
  not not_62 (not_62_out, and_3_out);
  not not_63 (not_63_out, and_4_out);
  not not_64 (not_64_out, and_5_out);
  not not_65 (not_65_out, and_6_out);
  not not_66 (not_66_out, and_7_out);
  not not_67 (not_67_out, and_8_out);
  and and_121 (and_121_out, d_ff_56_q, not_60_out);
  and and_122 (and_122_out, and_1_out, in_8);
  and and_123 (and_123_out, d_ff_57_q, not_61_out);
  and and_124 (and_124_out, and_2_out, in_8);
  and and_125 (and_125_out, d_ff_58_q, not_62_out);
  and and_126 (and_126_out, and_3_out, in_8);
  and and_127 (and_127_out, d_ff_59_q, not_63_out);
  and and_128 (and_128_out, and_4_out, in_8);
  and and_129 (and_129_out, d_ff_60_q, not_64_out);
  and and_130 (and_130_out, and_5_out, in_8);
  and and_131 (and_131_out, d_ff_61_q, not_65_out);
  and and_132 (and_132_out, and_6_out, in_8);
  and and_133 (and_133_out, d_ff_62_q, not_66_out);
  and and_134 (and_134_out, and_7_out, in_8);
  and and_135 (and_135_out, d_ff_63_q, not_67_out);
  and and_136 (and_136_out, and_8_out, in_8);
  D_Flip_Flop d_ff_56 (.D(or_57_out), .clk(Clock), .Q(d_ff_56_q));  // open: Qn, preset, reset
  or or_57 (or_57_out, and_121_out, and_122_out);
  D_Flip_Flop d_ff_57 (.D(or_58_out), .clk(Clock), .Q(d_ff_57_q));  // open: Qn, preset, reset
  or or_58 (or_58_out, and_123_out, and_124_out);
  D_Flip_Flop d_ff_58 (.D(or_59_out), .clk(Clock), .Q(d_ff_58_q));  // open: Qn, preset, reset
  or or_59 (or_59_out, and_125_out, and_126_out);
  D_Flip_Flop d_ff_59 (.D(or_60_out), .clk(Clock), .Q(d_ff_59_q));  // open: Qn, preset, reset
  or or_60 (or_60_out, and_127_out, and_128_out);
  D_Flip_Flop d_ff_60 (.D(or_61_out), .clk(Clock), .Q(d_ff_60_q));  // open: Qn, preset, reset
  or or_61 (or_61_out, and_129_out, and_130_out);
  D_Flip_Flop d_ff_61 (.D(or_62_out), .clk(Clock), .Q(d_ff_61_q));  // open: Qn, preset, reset
  or or_62 (or_62_out, and_131_out, and_132_out);
  D_Flip_Flop d_ff_62 (.D(or_63_out), .clk(Clock), .Q(d_ff_62_q));  // open: Qn, preset, reset
  or or_63 (or_63_out, and_133_out, and_134_out);
  D_Flip_Flop d_ff_63 (.D(or_64_out), .clk(Clock), .Q(d_ff_63_q));  // open: Qn, preset, reset
  or or_64 (or_64_out, and_135_out, and_136_out);
  assign controlled_buffer_56_out = Output_Ctrl ? d_ff_56_q : 1'bz;  // Controlled_Buffer controlled_buffer_56
  LED led_64 (.in(d_ff_56_q));
  assign controlled_buffer_56_out = Output_Ctrl_2 ? d_ff_57_q : 1'bz;  // Controlled_Buffer controlled_buffer_57
  LED led_65 (.in(d_ff_57_q));
  assign controlled_buffer_56_out = Output_Ctrl_3 ? d_ff_58_q : 1'bz;  // Controlled_Buffer controlled_buffer_58
  LED led_66 (.in(d_ff_58_q));
  assign controlled_buffer_56_out = Output_Ctrl_4 ? d_ff_59_q : 1'bz;  // Controlled_Buffer controlled_buffer_59
  LED led_67 (.in(d_ff_59_q));
  assign controlled_buffer_56_out = Output_Ctrl_5 ? d_ff_60_q : 1'bz;  // Controlled_Buffer controlled_buffer_60
  LED led_68 (.in(d_ff_60_q));
  assign controlled_buffer_56_out = Output_Ctrl_6 ? d_ff_61_q : 1'bz;  // Controlled_Buffer controlled_buffer_61
  LED led_69 (.in(d_ff_61_q));
  assign controlled_buffer_56_out = Output_Ctrl_7 ? d_ff_62_q : 1'bz;  // Controlled_Buffer controlled_buffer_62
  LED led_70 (.in(d_ff_62_q));
  assign controlled_buffer_56_out = Output_Ctrl_8 ? d_ff_63_q : 1'bz;  // Controlled_Buffer controlled_buffer_63
  LED led_71 (.in(d_ff_63_q));
  LED led_72 (.in(controlled_buffer_56_out));

  // Notes on the sheet:
  //   Address Decoder 3-8 with Enable
  //   RAM(8x8) with Address Decoder
endmodule
