// Logisim project Registers_and_ALU.circ as structural Verilog: 1 circuit, main circuit main
module main (
  input  Load,
  input  OC,
  input  Output_Ctrl,
  input  SUB,
  input  Clock,
  input  Load_B,
  input  Output_Ctrl_B,
  input  Clock_B,
  input  Load_C,
  input  in_10,
  input  Output_Ctrl_C,
  input  Clock_C,
  input  in_13,
  input  in_14,
  input  in_15
);

  wire and_1_out, and_2_out, and_3_out, and_4_out, and_5_out, and_6_out, and_7_out, and_8_out, and_9_out,
       and_10_out, and_11_out, and_12_out, and_13_out, and_14_out, and_15_out, and_16_out, and_17_out,
       and_18_out, and_19_out, and_20_out, and_21_out, and_22_out, and_23_out, and_24_out, and_25_out,
       and_26_out, and_27_out, and_28_out, and_29_out, and_30_out, and_31_out, and_32_out,
       controlled_buffer_1_out, controlled_buffer_2_out, controlled_buffer_3_out, controlled_buffer_4_out,
       controlled_buffer_5_out, controlled_buffer_6_out, controlled_buffer_7_out, controlled_buffer_8_out,
       controlled_buffer_9_out, controlled_buffer_10_out, controlled_buffer_15_out, d_ff_1_q, d_ff_2_q,
       d_ff_3_q, d_ff_4_q, d_ff_5_q, d_ff_6_q, d_ff_7_q, d_ff_8_q, d_ff_9_q, d_ff_10_q, D_Flip_Flop_B_q,
       D_Flip_Flop_q, not_1_out, not_2_out, not_3_out, not_4_out, not_5_out, not_6_out, not_7_out, not_8_out,
       not_9_out, not_10_out, not_11_out, not_12_out, or_1_out, or_2_out, or_3_out, or_4_out, or_5_out,
       or_6_out, or_7_out, or_8_out, or_9_out, or_10_out, or_11_out, or_12_out, or_13_out, or_14_out,
       or_15_out, or_16_out, tri_state_logic_B_out, tri_state_logic_out, xor_1_out, xor_2_out, xor_3_out,
       xor_4_out, xor_5_out, xor_6_out, xor_7_out, xor_8_out, xor_9_out, xor_10_out, xor_11_out, xor_12_out;

  and and_1 (and_1_out, d_ff_1_q, not_1_out);
  not not_1 (not_1_out, Load_C);
  and and_2 (and_2_out, Load_C, in_10);
  and and_3 (and_3_out, d_ff_2_q, not_2_out);
  not not_2 (not_2_out, Load_C);
  and and_4 (and_4_out, Load_C, in_13);
  and and_5 (and_5_out, d_ff_3_q, not_3_out);
  not not_3 (not_3_out, Load_C);
  and and_6 (and_6_out, Load_C, in_14);
  not not_4 (not_4_out, Load_C);
  or or_1 (or_1_out, and_1_out, and_2_out);
  and and_7 (and_7_out, d_ff_4_q, not_4_out);
  and and_8 (and_8_out, Load_C, in_15);
  D_Flip_Flop d_ff_1 (.D(or_1_out), .clk(Clock_C), .Q(d_ff_1_q));  // open: Qn, preset, reset
  or or_2 (or_2_out, and_3_out, and_4_out);
  or or_3 (or_3_out, and_5_out, and_6_out);
  or or_4 (or_4_out, and_7_out, and_8_out);
  assign controlled_buffer_1_out = Output_Ctrl_C ? d_ff_1_q : 1'bz;  // Controlled_Buffer controlled_buffer_1
  D_Flip_Flop d_ff_2 (.D(or_2_out), .clk(Clock_C), .Q(d_ff_2_q));  // open: Qn, preset, reset
  D_Flip_Flop d_ff_3 (.D(or_3_out), .clk(Clock_C), .Q(d_ff_3_q));  // open: Qn, preset, reset
  D_Flip_Flop d_ff_4 (.D(or_4_out), .clk(Clock_C), .Q(d_ff_4_q));  // open: Qn, preset, reset
  LED led_1 (.in(controlled_buffer_15_out));
  assign controlled_buffer_2_out = Output_Ctrl_C ? d_ff_2_q : 1'bz;  // Controlled_Buffer controlled_buffer_2
  assign controlled_buffer_3_out = Output_Ctrl_C ? d_ff_3_q : 1'bz;  // Controlled_Buffer controlled_buffer_3
  LED led_2 (.in(controlled_buffer_4_out));
  LED led_3 (.in(controlled_buffer_3_out));
  LED led_4 (.in(d_ff_1_q));
  assign controlled_buffer_4_out = Output_Ctrl_C ? d_ff_4_q : 1'bz;  // Controlled_Buffer controlled_buffer_4
  LED led_5 (.in(controlled_buffer_2_out));
  LED led_6 (.in(d_ff_2_q));
  LED led_7 (.in(d_ff_3_q));
  LED led_8 (.in(d_ff_4_q));
  LED led_9 (.in(controlled_buffer_1_out));
  not not_5 (not_5_out, Load);
  and and_9 (and_9_out, D_Flip_Flop_q, not_5_out);
  and and_10 (and_10_out, Load, controlled_buffer_1_out);
  not not_6 (not_6_out, Load);
  not not_7 (not_7_out, Load);
  and and_11 (and_11_out, D_Flip_Flop_B_q, not_8_out);
  not not_8 (not_8_out, Load_B);
  and and_12 (and_12_out, Load_B, controlled_buffer_1_out);
  and and_13 (and_13_out, d_ff_5_q, not_6_out);
  and and_14 (and_14_out, Load, controlled_buffer_2_out);
  and and_15 (and_15_out, d_ff_6_q, not_7_out);
  and and_16 (and_16_out, Load, controlled_buffer_3_out);
  and and_17 (and_17_out, d_ff_7_q, not_9_out);
  not not_9 (not_9_out, Load);
  and and_18 (and_18_out, Load, controlled_buffer_4_out);
  and and_19 (and_19_out, d_ff_8_q, not_10_out);
  not not_10 (not_10_out, Load_B);
  and and_20 (and_20_out, Load_B, controlled_buffer_2_out);
  and and_21 (and_21_out, d_ff_9_q, not_11_out);
  not not_11 (not_11_out, Load_B);
  and and_22 (and_22_out, Load_B, controlled_buffer_3_out);
  not not_12 (not_12_out, Load_B);
  D_Flip_Flop D_Flip_Flop (.D(or_5_out), .clk(Clock), .Q(D_Flip_Flop_q));  // open: Qn, preset, reset
  or or_5 (or_5_out, and_9_out, and_10_out);
  or or_6 (or_6_out, and_11_out, and_12_out);
  and and_23 (and_23_out, d_ff_10_q, not_12_out);
  and and_24 (and_24_out, Load_B, controlled_buffer_4_out);
  D_Flip_Flop d_ff_5 (.D(or_7_out), .clk(Clock), .Q(d_ff_5_q));  // open: Qn, preset, reset
  or or_7 (or_7_out, and_13_out, and_14_out);
  or or_8 (or_8_out, and_15_out, and_16_out);
  or or_9 (or_9_out, and_17_out, and_18_out);
  D_Flip_Flop D_Flip_Flop_B (.D(or_6_out), .clk(Clock_B), .Q(D_Flip_Flop_B_q));  // open: Qn, preset, reset
  or or_10 (or_10_out, and_19_out, and_20_out);
  or or_11 (or_11_out, and_21_out, and_22_out);
  or or_12 (or_12_out, and_23_out, and_24_out);
  assign tri_state_logic_out = Output_Ctrl ? D_Flip_Flop_q : 1'bz;  // Controlled_Buffer tri_state_logic
  D_Flip_Flop d_ff_6 (.D(or_8_out), .clk(Clock), .Q(d_ff_6_q));  // open: Qn, preset, reset
  D_Flip_Flop d_ff_7 (.D(or_9_out), .clk(Clock), .Q(d_ff_7_q));  // open: Qn, preset, reset
  assign tri_state_logic_B_out = Output_Ctrl_B ? D_Flip_Flop_B_q : 1'bz;  // Controlled_Buffer tri_state_logic_B
  D_Flip_Flop d_ff_8 (.D(or_10_out), .clk(Clock_B), .Q(d_ff_8_q));  // open: Qn, preset, reset
  D_Flip_Flop d_ff_9 (.D(or_11_out), .clk(Clock_B), .Q(d_ff_9_q));  // open: Qn, preset, reset
  D_Flip_Flop d_ff_10 (.D(or_12_out), .clk(Clock_B), .Q(d_ff_10_q));  // open: Qn, preset, reset
  assign controlled_buffer_5_out = Output_Ctrl ? d_ff_5_q : 1'bz;  // Controlled_Buffer controlled_buffer_5
  assign controlled_buffer_6_out = Output_Ctrl ? d_ff_6_q : 1'bz;  // Controlled_Buffer controlled_buffer_6
  assign controlled_buffer_7_out = Output_Ctrl ? d_ff_7_q : 1'bz;  // Controlled_Buffer controlled_buffer_7
  assign controlled_buffer_8_out = Output_Ctrl_B ? d_ff_8_q : 1'bz;  // Controlled_Buffer controlled_buffer_8
  assign controlled_buffer_9_out = Output_Ctrl_B ? d_ff_9_q : 1'bz;  // Controlled_Buffer controlled_buffer_9
  LED led_10 (.in(D_Flip_Flop_q));
  LED led_11 (.in(d_ff_5_q));
  LED led_12 (.in(d_ff_6_q));
  LED led_13 (.in(d_ff_7_q));
  LED led_14 (.in(D_Flip_Flop_B_q));
  assign controlled_buffer_10_out = Output_Ctrl_B ? d_ff_10_q : 1'bz;  // Controlled_Buffer controlled_buffer_10
  LED led_15 (.in(d_ff_8_q));
  LED led_16 (.in(d_ff_9_q));
  LED led_17 (.in(d_ff_10_q));
  xor xor_1 (xor_1_out, tri_state_logic_B_out, SUB);
  xor xor_2 (xor_2_out, controlled_buffer_8_out, SUB);
  xor xor_3 (xor_3_out, controlled_buffer_9_out, SUB);
  xor xor_4 (xor_4_out, controlled_buffer_10_out, SUB);
  xor xor_5 (xor_5_out, tri_state_logic_out, xor_1_out);
  and and_25 (and_25_out, tri_state_logic_out, xor_1_out);
  xor xor_6 (xor_6_out, controlled_buffer_5_out, xor_2_out);
  and and_26 (and_26_out, controlled_buffer_5_out, xor_2_out);
  xor xor_7 (xor_7_out, controlled_buffer_6_out, xor_3_out);
  and and_27 (and_27_out, controlled_buffer_6_out, xor_3_out);
  xor xor_8 (xor_8_out, controlled_buffer_7_out, xor_4_out);
  and and_28 (and_28_out, controlled_buffer_7_out, xor_4_out);
  xor xor_9 (xor_9_out, xor_5_out, SUB);
  and and_29 (and_29_out, xor_5_out, SUB);
  or or_13 (or_13_out, and_25_out, and_29_out);
  xor xor_10 (xor_10_out, xor_6_out, or_13_out);
  and and_30 (and_30_out, xor_6_out, or_13_out);
  or or_14 (or_14_out, and_26_out, and_30_out);
  xor xor_11 (xor_11_out, xor_7_out, or_14_out);
  and and_31 (and_31_out, xor_7_out, or_14_out);
  or or_15 (or_15_out, and_27_out, and_31_out);
  xor xor_12 (xor_12_out, xor_8_out, or_15_out);
  and and_32 (and_32_out, xor_8_out, or_15_out);
  or or_16 (or_16_out, and_28_out, and_32_out);
  LED led_18 (.in(xor_9_out));
  LED led_19 (.in(xor_10_out));
  LED led_20 (.in(xor_11_out));
  LED led_21 (.in(xor_12_out));
  LED led_22 (.in(or_16_out));
  assign controlled_buffer_1_out = OC ? xor_9_out : 1'bz;  // Controlled_Buffer controlled_buffer_11
  assign controlled_buffer_2_out = OC ? xor_10_out : 1'bz;  // Controlled_Buffer controlled_buffer_12
  assign controlled_buffer_3_out = OC ? xor_11_out : 1'bz;  // Controlled_Buffer controlled_buffer_13
  assign controlled_buffer_4_out = OC ? xor_12_out : 1'bz;  // Controlled_Buffer controlled_buffer_14
  assign controlled_buffer_15_out = OC ? or_16_out : 1'bz;  // Controlled_Buffer controlled_buffer_15

  // Notes on the sheet:
  //   REGISTER C
  //   BUS
  //   REGISTER A
  //   REGISTER B
  //   4 Bit Registers and a 4 Bit Adder
  //   4_Bit_Full_Adder
  //   NOTES
  //   SUB works both  as XOR control for inverting the B register bits, and also adding 1 (For two's complement) through carry in
endmodule
