// Logisim project XOR_Gate.circ as structural Verilog: 1 circuit, main circuit main
module main (
  input  A,
  input  B
);

  wire and_1_out, and_2_out, not_1_out, or_1_out;

  // XOR_Gate xor_1 is placed but not wired
  and and_1 (and_1_out, A, B);
  or or_1 (or_1_out, A, B);
  not not_1 (not_1_out, and_1_out);
  and and_2 (and_2_out, not_1_out, or_1_out);
  LED led_1 (.in(and_2_out));

  // Notes on the sheet:
  //   XOR Gate
  //   Diagram:
  //   truth table
  //   A      B    XOR
  //   0      0      0
  //   0      1      1
  //   1      0      1
  //   1      1      0
endmodule
